# Fritzing sketch pcb (saved by Fritzing 0.9.3b)
circuit board: 8.46667cm x 5.64444cm
breadboards: 1

parts:
  botRec = Pushbutton [package="[THT]"]
  C100µF = Electrolytic Capacitor [capacitance=100µF voltage=16V package="100 mil [THT, electrolytic]"]
  RFimRecol = Resistor [tolerance=±5% resistance=100 package=THT]
  RfimInje = Resistor [tolerance=±5% resistance=100 package=THT]
  R100Ω = Resistor [tolerance=±5% resistance=100 package=THT]
  BotIni = Momentary Switch [package=ksa_sealed_tac_switch]
  Nema14 = Stepper Motor - Bipolar
  driver = Pololu A4988 [package=SO16]
  botPa = Pushbutton [package="[THT]"]
  Lvm = LED - 3mm [color="Red (633nm)" package="3 mm [THT]"]
  RLver = Resistor [tolerance=±5% resistance=100 package=THT]
  LV = LED - 5mm [color="Green (570nm)" package="5 mm [THT]"]
  R3lVer = Resistor [tolerance=±5% resistance=100 package=THT]
  Buzzer = Piezo Speaker
  R100Ω_2 = Resistor [tolerance=±5% resistance=100 package=THT]
  R100Ω_3 = Resistor [tolerance=±5% resistance=100 package=THT]
  LM317 = Voltage Regulator [part_number=LM package=to220-adj]
  R68Ω = Resistor [tolerance=±5% resistance=68 package="2010 [SMD]"]
  R220Ω = Resistor [tolerance=±5% resistance=220 package="2010 [SMD]"]
  FCrec = Toggle Switch [package=THT]
  FCinj = Toggle Switch [package=THT]
  Part1 = Arduino Uno (Rev3)

nets:
  N1: botRec.Pin_1, botRec.Pin_2, R100Ω.Pin_0, Part1.D10_PWM/SS
  VDD: botRec.Pin_3, botRec.Pin_4, BotIni.4, driver.VDD, botPa.Pin_3, botPa.Pin_4, FCrec.L2, FCinj.L2, Part1.3V3
  N2: C100µF.-, driver.GND#14, LM317.ADJ, R68Ω.Pin_0, R220Ω.Pin_0
  N3: C100µF.+, driver.VMOT, LM317.OUT
  N4: RFimRecol.Pin_0, FCrec.COM, Part1.D8
  N5: RFimRecol.Pin_1, R100Ω.Pin_1, driver.GND#8, Lvm.cathode, LV.cathode, R100Ω_2.Pin_1, R100Ω_3.Pin_1, Part1.GND
  N6: RfimInje.Pin_0, FCinj.COM, Part1.D9_PWM
  N7: BotIni.2, R100Ω_3.Pin_0, Part1.D11_PWM/MOSI
  N8: Nema14.A, driver.2A
  N9: Nema14.C, driver.1A
  N10: Nema14.B, driver.1B
  N11: Nema14.D, driver.2B
  N12: driver.ENABLE, Part1.D5_PWM
  N13: driver.RESET, driver.SLEEP
  N14: driver.STEP, Part1.D4
  N15: driver.DIR, Part1.D3_PWM
  N16: botPa.Pin_1, botPa.Pin_2, R100Ω_2.Pin_0, Part1.D6_PWM
  N17: Lvm.anode, RLver.Pin_0, RLver.Pin_1, Part1.D7
  N18: LV.anode, R3lVer.Pin_0, R3lVer.Pin_1, Part1.D13/SCK
  N19: Buzzer.pin2, Part1.D12/MISO
  N20: LM317.IN, R68Ω.Pin_1

notes:
  Fonte 12V 1A
  capacitor eletrolitico 100uF
  Negativo plug
  5V

// code stored in the sketch: Untitled3.ino
//  MAQUINA INJETORA DE DIETA VIA SERINGA 60ML
//  BY JOÃO SANTOS 
//  https://www.linkedin.com/in/joaomarceloms
//  https://github.com/JoaoSantosBH/
//  joaomarcelo.ms@gmail.com
//  fev/2017
// A IMPLEMENTAR:
// 01- detectar torque do motor de giro para possivel entupimento do sistema E PAUSAR A MAQUINA
usando sensor de peso no empurrador do embolo

// VERSAO 1.0.0

//IMPORTANDO BIBLIOTECA MOTOR PASSO
#include <AccelStepper.h>

//DECLARANDO OS COMPONENTES DA MAQUINA INJETORA
int ledVerde                     = 13;
int buzzer                       = 12;
int botInjetar                   = 11;
int botRecolher                  = 10;
int fimCursoInjecaoCompleto      =  9;
int fimCursoRecolhimentoCompleto =  8;
int ledVermelho                  =  7;
int botParar                     =  6;

// Definicao pino ENABLE MOTOR PASSO
int pino_enable = 5;

// PINOS STEP e DIR MOTOR PASSO
AccelStepper motorPasso(1,4,3 );

//DEFINE QUANTIDADE GIROS DO MOTOR, 
//COMO TEMOS UM FIM DE CURSO IMPLEMENTEI UM NUMERO MUITO GRANDE DE VOLTAS
long passo = 1000000;

//VARIAVEIS QUE VAO DETECTAR O ESTADO DE CADA BOTAO
int estadoBotaoInje =        0;
int estadoBotaoRecolhe =     0;
int estadoBotaoParar =       0;

//VARIAVEIS QUE VAO DETECTAR O ESTADO DE CADA FIM DE CURSO
int estadoFimInjCompleto =   0;
int estadoFimRecolhimento =  0;

//VARIAVEL QUE DETECTA SE A MAQUINA ESTA EM FUNCIONAMENTO
int estaInjetando  = 0;
int estaAguardando = 1;
int estaRecolhendo = 0;

//detecta o tempo desde que o botão foi apertado
unsigned long changeTime; 

//DEFININDO O SETUP DOS COMPONENTES
void setup() {

pinMode(botInjetar,INPUT);
pinMode(botRecolher,INPUT);
pinMode(botParar, INPUT);
pinMode(fimCursoInjecaoCompleto, INPUT);
pinMode(fimCursoRecolhimentoCompleto,INPUT);                     
pinMode(ledVerde,OUTPUT);
pinMode(ledVermelho, OUTPUT);
pinMode(buzzer,OUTPUT);
pinMode(pino_enable, OUTPUT);

// Configuracoes iniciais motor de passo - INICIAR PARADO
motorPasso.move(0);
digitalWrite(pino_enable, HIGH);

apagarLedVermelho();
acenderLedVerde();
//INICIA COMUNICACAO SERIAL
Serial.begin(9600);
Serial.print("Maquina inicializada");
}


void loop() {

//LER ESTADO ATUA DOS COMPONENTES 
estadoBotaoInje         = digitalRead(botInjetar);
estadoBotaoRecolhe      = digitalRead(botRecolher); 
estadoBotaoParar        = digitalRead(botParar);
estadoFimInjCompleto    = digitalRead(fimCursoInjecaoCompleto);
estadoFimRecolhimento   = digitalRead(fimCursoRecolhimentoCompleto);


  //CASO BOTAO VERDE INICIAR APERTADO
  if (estadoBotaoInje == HIGH && (millis() - changeTime)> 5000){
       if(estaInjetando == 0 && estaAguardando ==1 && estaRecolhendo== 0){
          iniciarInjecao();
       }
    } 
  //CASO FIM DE CURSO INJECAO COMPLETA 
   if (estadoFimInjCompleto == HIGH && (millis() - changeTime)> 5000){
       if(estaInjetando == 1 && estaAguardando ==0 && estaRecolhendo== 0){
          pararMotorPassoInjecao();  
       }
    } 
 //CASO BOTAO AZUL RECOLHER APERTADO
   if (estadoBotaoRecolhe == HIGH && (millis() - changeTime)> 5000){
      if(estaInjetando == 0 && estaAguardando ==1 && estaRecolhendo== 0){
          recolherCursor();
        }
    }
 //CASO FIM DE CURSO RECOLHIMENTO COMPLETO 
    if (estadoFimRecolhimento == HIGH && (millis() - changeTime)> 5000){
       if(estaInjetando == 0 && estaAguardando ==0 && estaRecolhendo== 1){
          pararMotorPassoRecolhimento();  
       }
    }
 //CASO BOTAO VERMELHO PARAR APERTADO 
    if (estadoBotaoParar == HIGH && (millis() - changeTime)> 5000){
        if(estaInjetando == 1 && estaAguardando ==0 && estaRecolhendo== 0){
             pararMaquina();      
        }
    }
     
     motorPasso.run();
     
}

  
//F U N C O E S  D A   M A Q U I N A I  N J E T O R A

void acenderLedVerde(){
  digitalWrite(ledVerde, HIGH);
}
void apagarLedVerde(){
  digitalWrite(ledVerde,LOW);
}
void acenderLedVermelho(){
    digitalWrite(ledVermelho, HIGH);
}
void apagarLedVermelho(){
  digitalWrite(ledVermelho, LOW);
}


//INICIA A INJECAO
void iniciarInjecao(){
  estaInjetando  = 1;
  estaAguardando = 0; 
  estaRecolhendo = 0;
  Serial.println("INICIANDO INJECAO");
  apagarLedVerde();
  acenderLedVermelho();
  motorPasso.setMaxSpeed(150);
  motorPasso.setSpeed(150); 
  motorPasso.setAcceleration(150);//Novo
  digitalWrite(pino_enable, LOW);
  motorPasso.move(-passo);
  verificarStatus();
}

//INICIA O RECOLHIMENTO DO TRIlHO
void recolherCursor(){
  estaInjetando  = 0;
  estaAguardando = 0; 
  estaRecolhendo = 1;
  acenderLedVermelho();
  apagarLedVerde();
  Serial.println("RECOLHENDO CURSOR");
  digitalWrite(pino_enable, LOW);   
  motorPasso.setMaxSpeed(2000);
  motorPasso.setSpeed(2000);
  motorPasso.setAcceleration(2000);//Novo
  motorPasso.move(passo);
  verificarStatus();
}

//PARA INJECAO E EMITE ALERTA SONORO
void pararMotorPassoInjecao(){
  Serial.println("A INJECAO ACABOU");
  estaInjetando  = 0;
  estaAguardando = 1; 
  estaRecolhendo = 0;
  motorPasso.move(0);
  digitalWrite(pino_enable, HIGH);
  tocarBuz();
  acenderLedVerde();
  apagarLedVermelho();
  verificarStatus();
}

//PARA MAQUINA
void pararMaquina(){
  Serial.println(" MAQUINA PAUSADA");
  estaInjetando  = 0;
  estaAguardando = 1; 
  estaRecolhendo = 0;
  motorPasso.move(0);
  digitalWrite(pino_enable, HIGH);
  acenderLedVermelho();
  apagarLedVerde();
  verificarStatus();
}

// QUANDO ATINGE O FDC - PARA RECOLHIMENTO E EMITE ALERTA SONORO
void pararMotorPassoRecolhimento(){
  Serial.println("O RECOLHIMENTO CHEGOU AO FIM");
  tocarBuz();
  motorPasso.move(0);
  digitalWrite(pino_enable, HIGH);
  acenderLedVermelho();
  apagarLedVerde();
  delay(500);
  voltarUmPoquinho();
}

//FUNCAO QUE RECOLHE EMBOLO PARA NAO COLIDIR COM MOLA DO FIM DE CURSO
void voltarUmPoquinho(){
  Serial.println("INICIANDO RETORNO POSICAO ZERO");
  digitalWrite(pino_enable, LOW);
  motorPasso.move(-1000);
  estaInjetando  = 0;
  estaAguardando = 1; 
  estaRecolhendo = 0;
  apagarLedVermelho();
  acenderLedVerde();
  verificarStatus();
}

//VERIFICA STATUS CORRENTE DA MAQUINA
void verificarStatus(){
     if(estaRecolhendo == 1){
    Serial.println("Maquina esta Recolhendo");
    String message = (String) "BP = " + estadoBotaoParar +  ", EI = " + estaInjetando + ", EA = " + estaAguardando + ", ER = " + estaRecolhendo + " .";
    Serial.println(message );
     }
   if(estaInjetando == 1){
    Serial.println("Maquina esta Injetando");
    String message = (String) "BP = " + estadoBotaoParar +  ", EI = " + estaInjetando + ", EA = " + estaAguardando + ", ER = " + estaRecolhendo + " .";
    Serial.println(message );
   }
   if(estaAguardando == 1){
    Serial.println("Maquina esta Aguardando");
    String message = (String) "BP = " + estadoBotaoParar +  ", EI = " + estaInjetando + ", EA = " + estaAguardando + ", ER = " + estaRecolhendo + " .";
    Serial.println(message );
   }
}
// A L E R T A   S O N O R O
// THE IMPERIAL MARCH - John Williams
void tocarBuz(){   
  tone(buzzer,1500);   
  delay(500);
  noTone(buzzer);
  delay(50);
  tone(buzzer,1500);   
  delay(500);
  noTone(buzzer);
  delay(50);
  tone(buzzer,1500);   
  delay(500);
  noTone(buzzer);
  delay(50);
  tone(buzzer,1200);   
  delay(250);
  tone(buzzer,1850);   
  delay(250);
  noTone(buzzer);
  delay(50);
  tone(buzzer,1500);   
  delay(500);
  noTone(buzzer);
  delay(50);
  tone(buzzer,1200);   
  delay(250);
  tone(buzzer,1850);   
  delay(250);
  tone(buzzer,1500);   
  delay(500);
  noTone(buzzer);
  delay(500);
  ///////////////////
  tone(buzzer,2220);   
  delay(500);
  noTone(buzzer);
  delay(50);
  tone(buzzer,2220);   
  delay(500);
  noTone(buzzer);
  delay(50);
  tone(buzzer,2220);   
  delay(500); 
  tone(buzzer,2369);   
  delay(250);
  tone(buzzer,1850);   
  delay(250);
  noTone(buzzer);
  delay(50);
  tone(buzzer,1500);   
  delay(500);
  noTone(buzzer);
  delay(50);
  tone(buzzer,1200);   
  delay(250);
  tone(buzzer,1850);   
  delay(250);
  tone(buzzer,1500);   
  delay(500);
  noTone(buzzer);
}
//    T A B E L A   V E R D A D E   d o  S T A T U S da maquina
//
//  LEGENDA : Esta Injetando = EI  Esta Aguardando = EA   Esta Recolhendo = ER
//
// _______________________________  EI  | EA  | ER
// (00) ESTADO INICIAL DA MAQUINA |  0  |  1  |  0  |
//__________________________________________________|
// (01) INICIAR INJECAO           |  1  |  0  |  0  |
//__________________________________________________|
// (02) FIM CURSO ACABOU INJECAO  |  0  |  1  |  0  |
//__________________________________________________|
// (03) RECOLHER CURSOR           |  0  |  0  |  1  |
//__________________________________________________|
// (04) FIM CURSO RECOLHIMENTO    |  0  |  1  |  0  |
//__________________________________________________|
// (05) PAUSAR MAQUINA            |  0  |  1  |  0  |
//__________________________________________________|
