# Fritzing sketch maquinaInjetora (saved by Fritzing 0.9.3b)
circuit board: 8.46667cm x 5.64444cm
breadboards: 1

parts:
  botRecolher = Pushbutton [package="[THT]"]
  C1 = Electrolytic Capacitor [capacitance=100µF voltage=16V package="100 mil [THT, electrolytic]"]
  RFimRecol = Resistor [tolerance=±5% resistance=100 package=THT]
  RfimInje = Resistor [tolerance=±5% resistance=100 package=THT]
  RbotRecol = Resistor [tolerance=±5% resistance=100 package=THT]
  Part1 = Arduino Mega 2560 (Rev3)
  fimCursoRecolhimentoCompleto = Toggle Switch [package=THT]
  botIniciar = Momentary Switch [package=ksa_sealed_tac_switch]
  fimCursoInjecaoCompleto = Toggle Switch [package=THT]
  RbotInj = Resistor [tolerance=±5% resistance=100 package=THT]
  Nema14 = Stepper Motor - Bipolar
  Pololu_A1 = Pololu A4988 [package=SO16]
  botParar = Pushbutton [package="[THT]"]
  R1 = Resistor [tolerance=±5% resistance=100 package=THT]
  ledVermelho = LED - 3mm [color="Red (633nm)" package="3 mm [THT]"]
  R2 = Resistor [tolerance=±5% resistance=100 package=THT]
  ledVerde = LED - 5mm [color="Green (570nm)" package="5 mm [THT]"]
  R3 = Resistor [tolerance=±5% resistance=100 package=THT]
  Buzzer = Piezo Speaker

nets (from the breadboard view):
  N1: botRecolher.Pin_1, botRecolher.Pin_2, RbotRecol.Pin_0, Part1.D10_PWM
  3V3: botRecolher.Pin_3, botRecolher.Pin_4, Part1.3V3, fimCursoRecolhimentoCompleto.L2, botIniciar.4, fimCursoInjecaoCompleto.L2, Pololu_A1.VDD, botParar.Pin_3, botParar.Pin_4
  N2: C1.-, Pololu_A1.GND#14
  N3: C1.+, Pololu_A1.VMOT
  N4: RFimRecol.Pin_0, Part1.D8_PWM, fimCursoRecolhimentoCompleto.COM
  N5: RFimRecol.Pin_1, RbotRecol.Pin_1, Part1.GND, Part1.D6_PWM, RbotInj.Pin_1, Pololu_A1.GND#8, botParar.Pin_1, botParar.Pin_2, R1.Pin_0, R1.Pin_1, ledVermelho.cathode, ledVerde.cathode, Buzzer.pin1
  N6: RfimInje.Pin_0, Part1.D9_PWM, fimCursoInjecaoCompleto.COM
  N7: Part1.D13_PWM, ledVerde.anode, R3.Pin_0, R3.Pin_1
  N8: Part1.D12_PWM, Buzzer.pin2
  N9: Part1.D11_PWM, botIniciar.2, RbotInj.Pin_0
  N10: Part1.D3_PWM, Pololu_A1.DIR
  N11: Part1.D4_PWM, Pololu_A1.STEP
  N12: Part1.D5_PWM, Pololu_A1.ENABLE
  N13: Part1.D7_PWM, ledVermelho.anode, R2.Pin_0, R2.Pin_1
  N14: Nema14.A, Pololu_A1.2A
  N15: Nema14.C, Pololu_A1.1A
  N16: Nema14.B, Pololu_A1.1B
  N17: Nema14.D, Pololu_A1.2B
  N18: Pololu_A1.RESET, Pololu_A1.SLEEP

notes:
  Fonte 12V 1A
  capacitor eletrolitico 100uF
